# Fritzing sketch moscow_rfid (saved by Fritzing 0.9.3b)
breadboards: 3

parts:
  Part1 = Arduino Nano (Rev3.0) (ICSP)
  Part2 = RFID-RC522-v2
  U1 = 74HC595 [package="DIP16 [THT]"]
  U2 = 74HC595 [package="DIP16 [THT]"]
  R1 = Resistor [tolerance=±5% resistance=220 package="1206 [SMD]"]
  R2 = Resistor [tolerance=±5% resistance=220 package="1206 [SMD]"]
  R3 = Resistor [tolerance=±5% resistance=220 package="1206 [SMD]"]
  R4 = Resistor [tolerance=±5% resistance=220 package="1206 [SMD]"]
  R5 = Resistor [tolerance=±5% resistance=220 package="1206 [SMD]"]
  R6 = Resistor [tolerance=±5% resistance=220 package="1206 [SMD]"]
  R7 = Resistor [tolerance=±5% resistance=220 package="1206 [SMD]"]
  R8 = Resistor [tolerance=±5% resistance=220 package="1206 [SMD]"]
  IC1 = IC, DIP package, 12 pins [chip_label="4dig LED"]

nets:
  GND: Part1.GND, Part2.GND, U1.GND, U1.OE, U2.GND, U2.OE, R8.Pin_1, IC1.pin12
  N1: Part1.D2, U1.DS
  N2: Part1.D3, U1.ST_CP, U2.ST_CP
  N3: Part1.D4, U1.SH_CP, U2.SH_CP
  N4: Part1.D9, Part2.RST
  N5: Part1.D10, Part2.SDA
  N6: Part1.D11/MOSI, Part2.MOSI
  N7: Part1.D12/MISO, Part2.MISO
  VCC: Part1.5V, U1.MR, U1.VCC, U2.MR, U2.VCC
  3V3: Part1.3V3, Part2.3.3V
  N8: Part1.D13/SCK, Part2.SCK
  N9: U1.Q5, IC1.pin6
  N10: U1.Q6, IC1.pin8
  N11: U1.Q7, IC1.pin9
  N12: U1.Q7', U2.DS
  N13: U2.Q1, R1.Pin_1
  N14: U2.Q2, R2.Pin_1
  N15: U2.Q3, R3.Pin_1
  N16: U2.Q4, R4.Pin_1
  N17: U2.Q5, R5.Pin_1
  N18: U2.Q6, R6.Pin_1
  N19: U2.Q7, R7.Pin_1
  N20: R1.Pin_0, IC1.pin11
  N21: R2.Pin_0, IC1.pin7
  N22: R3.Pin_0, IC1.pin4
  N23: R4.Pin_0, IC1.pin2
  N24: R5.Pin_0, IC1.pin1
  N25: R6.Pin_0, IC1.pin10
  N26: R7.Pin_0, IC1.pin5
  N27: R8.Pin_0, IC1.pin3

notes:
  12-pin IC on the right side of this note represents pinout of a typical 4 digit LED display.
  Pins 6, 8, 9 and 12 select the digits.
  Other pins control individual segments.

custom parts:
  RFID-RC522-v2: A simple China made RFID-RC522 Reader; do check the pin labels, as this is a MFRC522 based clone.
